# Fritzing sketch ShuiGuanPipe (saved by Fritzing 1.0.3b)
circuit board: 9.00001cm x 5.68cm
breadboards: 1

parts:
  J2 = Generic single row SMD female header - 30 pins [form="♀ (female)" package=THT]
  J3 = Generic single row SMD female header - 30 pins [form="♀ (female)" package=THT]  # not connected
  D1 = Rectifier Diode [part_number=1N4001 package="300 mil [THT]"]
  1_8K = Resistor [tolerance=±5% resistance=220 power=0.25W package=THT]
  74LS161 = IC, DIP package, 16 pins [chip_label=IC]
  74LS157 = IC, DIP package, 16 pins [chip_label=IC]
  74LS157_2 = IC, DIP package, 16 pins [chip_label=IC]
  AX5208C_/_VRC4 = IC, DIP package, 40 pins [chip_label=IC]
  100p = Ceramic Capacitor [capacitance=100nF package="200 mil [THT, multilayer]"]
  27C1 = 27C020 [chip_label=27C020]
  27C2 = 27C020 [chip_label=27C020]

nets:
  N1: J2.pin2, 27C1.connector24
  N2: J2.pin3, 27C1.connector22
  N3: J2.pin5, 27C1.connector26
  N4: J2.pin6, 27C1.connector4
  N5: J2.pin7, 27C1.connector5
  N6: J2.pin8, 27C1.connector6
  N7: J2.pin9, 27C1.connector7
  N8: J2.pin10, 74LS161.pin6, AX5208C_/_VRC4.pin3, 27C1.connector8
  N9: J2.pin11, 74LS161.pin5, AX5208C_/_VRC4.pin4, 27C1.connector9
  N10: J2.pin12, 74LS161.pin4, 27C1.connector10
  N11: J2.pin13, 74LS161.pin3, 27C1.connector11
  N12: J2.pin14, 74LS161.pin9, AX5208C_/_VRC4.pin9
  N13: J2.pin15, AX5208C_/_VRC4.pin17
  N14: J2.pin17, AX5208C_/_VRC4.pin12
  N15: J2.pin18, AX5208C_/_VRC4.pin13
  N16: J2.pin19, 27C2.connector5
  N17: J2.pin20, 27C2.connector6
  N18: J2.pin21, 27C2.connector7
  N19: J2.pin22, 27C2.connector8
  N20: J2.pin23, 27C2.connector9
  N21: J2.pin24, 27C2.connector10
  N22: J2.pin25, 27C2.connector11
  N23: J2.pin26, 27C2.connector12
  N24: J2.pin27, 27C2.connector13
  N25: J2.pin28, 27C2.connector14
  N26: J2.pin29, 27C2.connector16
  N27: D1.cathode, 1_8K.Pin_0, 74LS161.pin2, 100p.1
  N28: D1.anode, 1_8K.Pin_1, 74LS157_2.pin10, AX5208C_/_VRC4.pin19
  N29: 74LS161.pin7, 74LS161.pin10, 74LS157.pin13, 74LS157.pin16, 74LS157_2.pin6, 74LS157_2.pin15, 100p.0
  N30: 74LS161.pin11, 74LS157_2.pin3
  N31: 74LS161.pin12, 74LS157.pin10
  N32: 74LS161.pin13, 74LS157.pin6
  N33: 74LS161.pin14, 74LS157.pin3
  N34: 74LS157.pin2, AX5208C_/_VRC4.pin35
  N35: 74LS157.pin4, 27C1.connector27
  N36: 74LS157.pin5, AX5208C_/_VRC4.pin36
  N37: 74LS157.pin7, 27C1.connector28
  N38: 74LS157.pin9, 27C1.connector2
  N39: 74LS157.pin11, AX5208C_/_VRC4.pin38
  N40: 74LS157.pin12, AX5208C_/_VRC4.pin37
  N41: 74LS157_2.pin2, AX5208C_/_VRC4.pin34
  N42: 74LS157_2.pin4, 27C1.connector1
  N43: 74LS157_2.pin5, AX5208C_/_VRC4.pin39
  N44: 74LS157_2.pin7, 27C1.connector29
  N45: 74LS157_2.pin9, 27C1.connector21
  N46: 74LS157_2.pin11, AX5208C_/_VRC4.pin8
  N47: AX5208C_/_VRC4.pin10, 27C2.connector21
  N48: AX5208C_/_VRC4.pin21, 27C2.connector22
  N49: AX5208C_/_VRC4.pin22, 27C2.connector1
  N50: AX5208C_/_VRC4.pin23, 27C2.connector24
  N51: AX5208C_/_VRC4.pin24, 27C2.connector27
  N52: AX5208C_/_VRC4.pin25, 27C2.connector28
  N53: AX5208C_/_VRC4.pin26, 27C2.connector3
  N54: AX5208C_/_VRC4.pin27, 27C2.connector2

notes:
  水管PIPE Repro PCB. Designed by HeeminYT
  wtf??

custom parts:
  Generic single row SMD female header - 30 pins: Generic single row SMD female header
